# Fritzing sketch greenpithumb (saved by Fritzing 0.9.3b)
breadboards: 1

parts:
  Q1 = MOSFET-NCHANNEL [package=to220v]
  R1 = Resistor [tolerance=±5% resistance=10k package=THT]
  Raspberry_Pi_1 = Raspberry Pi 3 [part_number=RPI-3-V1.2]
  Power_plug1 = Power plug
  IC1 = MCP3008 8-channel 10-bit ADC [part_number=MCP3008]
  PART1 = SparkFun Soil Moisture Sensor [part_number=SEN-13322]
  DHT1 = DHT11 Humitidy and Temperature Sensor
  R2 = Resistor [tolerance=±5% resistance=10k package=THT]
  R3 = Photocell (LDR) [package=THT]
  R4 = Resistor [tolerance=±5% resistance=10k package=THT]
  R5 = Resistor [tolerance=±5% resistance=56k package=THT]
  R6 = Resistor [tolerance=±5% resistance=100 package=THT]
  M1 = DC Motor
  R7 = Resistor [tolerance=±5% resistance=56k package=THT]

nets:
  N1: Q1.G, R1.Pin_1, R7.Pin_0
  N2: Q1.D, M1.pin_2
  GND: Q1.S, Raspberry_Pi_1.GND, Power_plug1.GND, IC1.no_name_yet#9, DHT1.GND, R7.Pin_1
  N3: R1.Pin_0, Raspberry_Pi_1.GPIO26
  3V3: Raspberry_Pi_1.3v3, Raspberry_Pi_1.3V3, IC1.no_name_yet#15, IC1.no_name_yet#16, DHT1.VDD, R2.Pin_0, R3.pin_1
  N4: Raspberry_Pi_1.GPIO21, DHT1.DATA, R2.Pin_1
  N5: Raspberry_Pi_1.GPIO16, R5.Pin_1
  N6: Raspberry_Pi_1.GPIO12, R6.Pin_1
  N7: Raspberry_Pi_1.GPIO25, IC1.no_name_yet#10
  N8: Raspberry_Pi_1.GPIO24, IC1.no_name_yet#11
  N9: Raspberry_Pi_1.GPIO23, IC1.no_name_yet#12
  N10: Raspberry_Pi_1.GPIO18, IC1.no_name_yet#13
  N11: Power_plug1.VCC, M1.pin_1
  N12: IC1.no_name_yet#1, R3.pin_0, R4.Pin_0
  N13: IC1.no_name_yet#8, PART1.SIG, R5.Pin_0
  N14: PART1.VCC, R6.Pin_0

custom parts:
  SparkFun Soil Moisture Sensor: The SparkFun Soil Moisture Sensor is a simple breakout for measuring the moisture in soil and similar materials.
  DHT11 Humitidy and Temperature Sensor: DHT11 Humidity and Temperature Sensor
